# Fritzing sketch HomeAtion_RemoteDHT_Design (saved by Fritzing 0.9.2b)
perfboards: 1

parts:
  R1 = Resistor [tolerance=±5% resistance=10k package=THT]  # not connected
  POWER_5V = male pin header, 5 pins [form="♂ (male)"]  # not connected
  C1 = male pin header, 2 pins [form="♂ (male)"]  # not connected
  C2 = male pin header, 2 pins [form="♂ (male)"]  # not connected
  LDO_3_3V = male pin header, 3 pins [form="♂ (male)"]  # not connected
  ESP8266 = female pin header, 4 pins [form="♀ (female)"]
  DHT22 = female pin header, 4 pins [form="♀ (female)"]  # not connected
  Debug = female pin header, 3 pins [form="♀ (female)"]  # not connected
  J4 = female pin header, 4 pins [form="♀ (female)"]  # not connected
  GPIO_0 = female pin header, 4 pins [form="♀ (female)"]

nets:
  N1: ESP8266.pin2, GPIO_0.pin2
