# Fritzing sketch programator (saved by Fritzing 0.9.2b)

parts:
  3V3_Power = Power plug
  U1 = ESP8266 WiFi Module [part_number=ESP8266]
  USB-Serial = female pin header, 3 pins [form="♀ (female)"]
  S1 = Pushbutton [package="[THT]"]

nets:
  VCC: 3V3_Power.VCC, U1.VCC, U1.CH_PD
  GND: 3V3_Power.GND, U1.GND, USB-Serial.pin3, S1.Pin_4
  N1: U1.RXD, USB-Serial.pin2
  N2: U1.GPIO_0, S1.Pin_1, S1.Pin_2
  N3: U1.TXD, USB-Serial.pin1

custom parts:
  ESP8266 WiFi Module: Generic WiFi Module based on the ESP8266 with onboard PCB antenna and UART communications
